# Fritzing sketch StairsV1 (saved by Fritzing 0.9.2b)
circuit board: 8.46667cm x 5.64444cm
breadboards: 1

parts:
  Q1 = Basic FET P-Channel [package="TO220 [THT]"]
  Q2 = Basic FET P-Channel [package="TO220 [THT]"]
  R1 = Resistor [tolerance=±5% resistance=220 package=THT]
  R2 = Resistor [tolerance=±5% resistance=220 package=THT]
  Súčiastka1 = Arduino Nano (Rev3.0)
  LDR_in = screw terminal, 3 pins
  Vcc = screw terminal, 2 pins
  PIRs = screw terminal, 5 pins
  LED_out = screw terminal, 3 pins

nets:
  N1: Q1.gate, Súčiastka1.D9
  N2: Q1.drain, LED_out.pin2
  N3: Q1.source, Q2.source, Vcc.pin2
  N4: Q2.gate, Súčiastka1.D10
  N5: Q2.drain, LED_out.pin3
  N6: R1.Pin_0, R2.Pin_0, Súčiastka1.GND, PIRs.pin2
  N7: R1.Pin_1, Súčiastka1.A1, LDR_in.pin3
  N8: R2.Pin_1, Súčiastka1.A2, LDR_in.pin2
  N9: Súčiastka1.D3, PIRs.pin3
  N10: Súčiastka1.D4, PIRs.pin4
  N11: Súčiastka1.D5, PIRs.pin5
  N12: Súčiastka1.VIN, Vcc.pin1, PIRs.pin1, LED_out.pin1
  N13: Súčiastka1.5V, LDR_in.pin1
